# Fritzing sketch wirelessUltrasonic_Schematic (saved by Fritzing 0.9.3b)

parts:
  Part1 = NRF24L01+ Breakout Board
  hc-sr1 = hc-sr04
  Part3 = Arduino Uno (Rev3) - ICSP
  Raspberry_Pi_1 = Raspberry Pi 3 [part_number=RPI-3-V1.2]
  Part2 = NRF24L01+ Breakout Board

nets:
  GND: Part1.GND, hc-sr1.GND, Part3.GND
  VCC: Part1.VCC, Part3.3V3
  N1: Part1.CE, Part3.D9_PWM
  N2: Part1.CS, Part3.D10_PWM/SS
  N3: Part1.SCK, Part3.D13/SCK
  N4: Part1.MOSI, Part3.D11_PWM/MOSI
  N5: Part1.MISO, Part3.ICSP_MISO, Part3.D12/MISO
  VCC_2: hc-sr1.VCC, Part3.5V
  N6: hc-sr1.Trig, Part3.D3_PWM
  N7: hc-sr1.Echo, Part3.D2
  3V3: Raspberry_Pi_1.3v3, Part2.VCC
  N8: Raspberry_Pi_1.GPIO22, Part2.CE
  N9: Raspberry_Pi_1.GPIO10, Part2.MOSI
  N10: Raspberry_Pi_1.GPIO9, Part2.MISO
  N11: Raspberry_Pi_1.GPIO11, Part2.SCK
  N12: Raspberry_Pi_1.GPIO8, Part2.CS
  GND_2: Raspberry_Pi_1.GND, Part2.GND

notes:
  RPi 3B+
